# Fritzing sketch recording_box (saved by Fritzing 0.9.4)
breadboards: 1

parts:
  Raspberry_Pi_1 = Raspberry Pi 3 [part_number=RPI-3-V1.2]
  U1 = LCD-16X2 [package=lcd-16x2]
  S2 = Momentary Switch [package=ksa_sealed_tac_switch]
  S3 = Momentary Switch [package=ksa_sealed_tac_switch]
  S1 = Momentary Switch [package=ksa_sealed_tac_switch]
  LED1 = LED - 5mm [color="Red (633nm)" package="5 mm [THT]"]
  LED2 = LED - 5mm [color="Green (555nm)" package="5 mm [THT]"]
  LED3 = LED - 5mm [color="White (4500K)" package="5 mm [THT]"]
  LCM1602_IIC1 = LCM1602 IIC [part_number="LCM1602 IIC" chip_label="LCM1602 IIC" package="DIP (Dual Inline) [THT]"]
  R1 = Resistor [tolerance=±5% resistance=1k package="2512 [SMD]"]
  R2 = Resistor [tolerance=±5% resistance=1k package="2512 [SMD]"]
  R3 = Resistor [tolerance=±5% resistance=1k package="2512 [SMD]"]
  Part1 = Adafruit PiRTC PCF8523 [part_number="Adafruit #3386"]

nets:
  3V3: Raspberry_Pi_1.3v3, Part1.3.3V
  N1: Raspberry_Pi_1.GPIO2, LCM1602_IIC1.SDA, Part1.SDA
  N2: Raspberry_Pi_1.GPIO3, LCM1602_IIC1.SCL, Part1.SCL
  N3: Raspberry_Pi_1.GPIO4, S1.2
  N4: Raspberry_Pi_1.GPIO22, S2.2
  GND: Raspberry_Pi_1.GND, S2.4, S3.4, S1.4, LCM1602_IIC1.GND, R1.Pin_1, R2.Pin_1, R3.Pin_1, Part1.GND
  N5: Raspberry_Pi_1.GPIO24, LED1.anode
  N6: Raspberry_Pi_1.GPIO23, S3.2
  5V: Raspberry_Pi_1.5V, LCM1602_IIC1.VCC
  VSS: U1.VSS, LCM1602_IIC1.VSS
  VDD: U1.VDD, LCM1602_IIC1.VDD
  N7: U1.VO, LCM1602_IIC1.V0
  N8: U1.RS, LCM1602_IIC1.RS
  N9: U1.R_W, LCM1602_IIC1.RW
  N10: U1.E, LCM1602_IIC1.E
  N11: U1.DB0, LCM1602_IIC1.D0
  N12: U1.DB1, LCM1602_IIC1.D1
  N13: U1.DB2, LCM1602_IIC1.D2
  N14: U1.DB3, LCM1602_IIC1.D3
  N15: U1.DB4, LCM1602_IIC1.D4
  N16: U1.DB5, LCM1602_IIC1.D5
  N17: U1.DB6, LCM1602_IIC1.D6
  N18: U1.DB7, LCM1602_IIC1.D7
  N19: U1.A, LCM1602_IIC1.A
  N20: U1.K, LCM1602_IIC1.K
  N21: LED1.cathode, R1.Pin_0
  N22: LED2.cathode, R2.Pin_0
  N23: LED3.cathode, R3.Pin_0

custom parts:
  LCM1602 IIC: I2C-Module to use a 1602 or 2004 LCD on with the wire.h libory Serial LCD Modul
  Adafruit PiRTC PCF8523: This is a great battery-backed real time clock (RTC) that allows your Raspberry Pi project to keep track of time if the power is lost. Perfect for data-logging, clock-building, time-stamping, timers and alarms, etc. Equipped with PCF8523 RTC, it works great with the Raspberry Pi and has native kernel support. Works perfectly with any Raspberry Pi (or similar single board linux computer)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
